# Fritzing sketch parkingsensor (saved by Fritzing 0.8.7b)
breadboards: 1

parts:
  Eleman1 = Arduino Uno (Rev3)
  R1 = Resistor [tolerance=±5% resistance=330 package=THT]
  R2 = Resistor [tolerance=±5% resistance=330 package=THT]
  R3 = Resistor [tolerance=±5% resistance=330 package=THT]
  R4 = Resistor [tolerance=±5% resistance=330 package=THT]
  R5 = Resistor [tolerance=±5% resistance=330 package=THT]
  R6 = Resistor [tolerance=±5% resistance=330 package=THT]
  R7 = Resistor [tolerance=±5% resistance=330 package=THT]
  LED1 = LED - 5mm [color="Green (555nm)" package="5 mm [THT]"]
  LED2 = LED - 5mm [color="Green (555nm)" package="5 mm [THT]"]
  LED3 = LED - 5mm [color="Yellow (595nm)" package="5 mm [THT]"]
  LED4 = LED - 5mm [color="Yellow (595nm)" package="5 mm [THT]"]
  LED5 = LED - 5mm [color="Red (633nm)" package="5 mm [THT]"]
  LED6 = LED - 5mm [color="Red (633nm)" package="5 mm [THT]"]
  U1 = HC-SR04 [chip_label=IC package="SIP (Single Inline) [THT]"]
  J1 = Piezo Speaker

nets:
  N1: Eleman1.D8, U1.Echo
  N2: Eleman1.D9_PWM, U1.Trig
  N3: Eleman1.D10_PWM/SS, R1.Pin_1
  GND: Eleman1.GND, LED1.cathode, LED2.cathode, LED3.cathode, LED4.cathode, LED5.cathode, LED6.cathode, U1.GND
  N4: Eleman1.D2, R5.Pin_0
  N5: Eleman1.D3_PWM, R4.Pin_0
  N6: Eleman1.D4, R6.Pin_0
  N7: Eleman1.D5_PWM, R7.Pin_0
  N8: Eleman1.D6_PWM, R3.Pin_0
  N9: Eleman1.D7, R2.Pin_0
  5V: Eleman1.5V, U1.Vcc
  N10: R1.Pin_0, J1.pin2
  N11: R2.Pin_1, LED1.anode
  N12: R3.Pin_1, LED2.anode
  N13: R4.Pin_1, LED5.anode
  N14: R5.Pin_1, LED6.anode
  N15: R6.Pin_1, LED4.anode
  N16: R7.Pin_1, LED3.anode

custom parts:
  HC-SR04: HC-SR04 ultrasound distance sensor
